# Fritzing sketch Ard-wifi_Bartender (saved by Fritzing 1.0.3b)
breadboards: 1

parts:
  HC-SR04_Sensor_1 = HC-SR04 Ultrasonic Distance Sensor
  M1 = DC Motor [voltage_(max)=6V voltage_(min)=3V]  # not connected
  M2 = DC Motor [voltage_(max)=6V voltage_(min)=3V]  # not connected
  M3 = DC Motor [voltage_(max)=6V voltage_(min)=3V]  # not connected
  M4 = DC Motor [voltage_(max)=6V voltage_(min)=3V]  # not connected
  M5 = DC Motor [voltage_(max)=6V voltage_(min)=3V]  # not connected
  M6 = DC Motor [voltage_(max)=6V voltage_(min)=3V]  # not connected
  M7 = DC Motor [voltage_(max)=6V voltage_(min)=3V]  # not connected
  M8 = DC Motor [voltage_(max)=6V voltage_(min)=3V]  # not connected
  M9 = DC Motor [voltage_(max)=6V voltage_(min)=3V]  # not connected
  M10 = DC Motor [voltage_(max)=6V voltage_(min)=3V]  # not connected
  M11 = DC Motor [voltage_(max)=6V voltage_(min)=3V]  # not connected
  M12 = DC Motor [voltage_(max)=6V voltage_(min)=3V]  # not connected
  A1 = Arduino UNO R4 WiFi
  U1 = 16-Channel Relay Module [package=relay-16ch]
  HX711_Weight_Sensor = Sparkfun load cell amplifier
  A2 = Hanmatek HM305
  J1 = Piezo Speaker
  A3 = yf-s401 flow sensor [package=THT]
  OLED_I2C1 = OLED 128x64 I2C Monochrome Display

nets:
  N1: HC-SR04_Sensor_1.TRIG, A1.Pin_45
  N2: HC-SR04_Sensor_1.ECHO, A1.Pin_44
  GND: HC-SR04_Sensor_1.GND, A1.Pin_9, A1.Pin_18, A1.Pin_48, U1.GND, U1.OUT_GND, HX711_Weight_Sensor.Pin_6, A2.Pin_3, J1.pin1, A3.pin2, OLED_I2C1.GND
  N3: A1.Pin_8, A1.Pin_27, U1.VCCOUT_5V, HX711_Weight_Sensor.Pin_9, HX711_Weight_Sensor.Pin_10, A3.pin1, OLED_I2C1.VDD
  N4: A1.Pin_40, OLED_I2C1.SDA
  N5: A1.Pin_41, OLED_I2C1.SCK
  N6: A1.Pin_42, HX711_Weight_Sensor.Pin_8
  N7: A1.Pin_43, HX711_Weight_Sensor.Pin_7
  N8: A1.Pin_47, A3.pin3
  N9: U1.VCC, A2.Pin_4

custom parts:
  Arduino UNO R4 WiFi: The Arduino UNO R4 WiFi merges the RA4M1 microprocessor from Renesas with the ESP32-S3 from Espressif, creating an all-in-one tool for makers with enhanced processing power and a diverse array of new peripherals.
  16-Channel Relay Module: 16 channel relay module
  Sparkfun load cell amplifier: The SparkFun Load Cell Amplifier is a small breakout board for the HX711 IC that allows you to easily read load cells to measure weight.
  Hanmatek HM305: DC Power Supply 30V5A HM305.
  yf-s401 flow sensor: Flow sensors sit in line with your water line, and uses a pinwheel sensor to measure how much liquid has moved through it.

// code stored in the sketch: Ard-wifi_Bartender.ino
//  Libraries 

//  GPIO
const flowRateSensor = 13;
const passiveBuzzer = 12 ;
const sonic_trig = 11;
const sonic_echo = 10;
const weight_clk = 9;
const weight_dat = 8;
const LED = pin;
const powerRelay = pin;
const pump = pin;



void setup() {
// machine is plugged in
// machine boots - yellow led?
// machine is waiting - green led
// --webserver booted.


}


void loop() {
// Wait for user to connect
// user connects to webserver
// Webserver instructs user to select a cup and place under dispenser 
// weight sensor checks: 'cup weight empty'
// ultrasonic sensor checks: 'cup height empty' 
// Webserver displays cup size, then displays the available drink options
// user selects beverage
// pump begins to pump
// flow rate sensor checks amount dispensed
// ultrasonic checks liquid height
// weight sensor stops process if cup is removed


}
